# Fritzing sketch GripperSketch (saved by Fritzing 0.8.7b)
breadboards: 2

parts:
  Part1 = Arduino Nano (Rev3.0)
  L298 = L298N DC motor driver
  Gripper_motor = Stepper Motor - Bipolar
  "EStop" = Toggle Switch [package=THT]
  LM2596_(24v_to_5v) = LM2596 step down module
  24v_input_--> = mystery part, 3 pins [chip_label=?]
  LM2596_(24v_to_12v) = LM2596 step down module
  Momentary_btn = Round Pushbutton
  35v_390uf = Capacitor Polarized [package=panasonic_c]
  Force_sensing_resistor = Basic Force Sensing Resistor (FSR) [package=THT]
  R1 = Resistor [tolerance=±5% resistance=220 package=THT]

nets:
  N1: Part1.GND, "EStop".COM, LM2596_(24v_to_5v).IN-, LM2596_(24v_to_5v).OUT-, Momentary_btn.leg0, R1.Pin_1
  N2: Part1.D2, L298.IN1
  N3: Part1.D3, L298.IN2
  N4: Part1.D4, L298.IN3
  N5: Part1.D5, L298.IN4
  N6: Part1.D7, "EStop".L2
  N7: Part1.D12/MISO, Momentary_btn.leg1
  VIN: Part1.VIN, L298.5V, LM2596_(24v_to_5v).OUT+
  N8: Part1.5V, Force_sensing_resistor.pin_0
  N9: Part1.A0, Force_sensing_resistor.pin_1, R1.Pin_0
  N10: L298.OUT1, Gripper_motor.C
  N11: L298.OUT2, Gripper_motor.A
  N12: L298.OUT3, Gripper_motor.B
  N13: L298.OUT4, Gripper_motor.D
  N14: L298.12V, LM2596_(24v_to_12v).OUT+
  N15: L298.GND, 24v_input_-->.pin1, LM2596_(24v_to_12v).IN-, LM2596_(24v_to_12v).OUT-, 35v_390uf.+, 35v_390uf.-
  N16: LM2596_(24v_to_5v).IN+, 24v_input_-->.pin3

custom parts:
  L298N DC motor driver: 2x DC motor driver with 78M05 positive voltage regulator (7..35 V) L298N: max 46 V, 2 A Set 5 V Enable jumper to enable 5 V regultor (needed for the L298N) and +5 V output at screw terminal or supply external +5 V at screw terminal Set ENA and/or ENB to +5 V to enable motor permanently or supply ENA and/or ENB with PWM signal IN1 and IN2 set rotation directory for motor A (OUT1/OUT2) IN2 and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
  LM2596 step down module: LM2596 DC-DC step down power supply module 3 A.
